// Logisim project CPU.circ as structural Verilog
module ALU (
  input  S0,
  input  S1,
  input  [7:0] A,
  input  [7:0] B,
  output CF,
  output [7:0] O
);

  wire n74139_1_pin1, n74139_1_pin4, n74139_1_pin6, n74139_1_pin7;
  wire [7:0] add_1_z, and8_1_z, invert_1_z;

  _74139 #(.ShowInternalStructure("true")) u_74139_1 (
    .pin1(n74139_1_pin1), .pin2(S0), .pin3(S1), .pin4(n74139_1_pin4), .pin5(n74139_1_pin4),
    .pin6(n74139_1_pin6), .pin7(n74139_1_pin7));  // open: pin15, pin14, pin13, pin12, pin11, pin10, pin9
  INVERT invert_1 (.EN(S0), .X(B), .Z(invert_1_z));
  ADD add_1 (.X(A), .Y(invert_1_z), .CIN(S0), .Z(add_1_z), .CF(CF));
  AND8 and8_1 (.A(A), .B(B), .Z(and8_1_z));
  _74244 #(.ShowInternalStructure("true")) u_74244_1 (
    .pin1(n74139_1_pin4), .pin2(add_1_z[7]), .pin3(O[0]), .pin4(add_1_z[6]), .pin5(O[1]), .pin6(add_1_z[5]),
    .pin7(O[2]), .pin8(add_1_z[4]), .pin9(O[3]), .pin19(n74139_1_pin4), .pin18(O[7]), .pin17(add_1_z[0]),
    .pin16(O[6]), .pin15(add_1_z[1]), .pin14(O[5]), .pin13(add_1_z[2]), .pin12(O[4]), .pin11(add_1_z[3]));
  _74240 #(.ShowInternalStructure("true")) u_74240_1 (
    .pin1(n74139_1_pin6), .pin2(A[7]), .pin3(O[0]), .pin4(A[6]), .pin5(O[1]), .pin6(A[5]), .pin7(O[2]),
    .pin8(A[4]), .pin9(O[3]), .pin19(n74139_1_pin6), .pin18(O[7]), .pin17(A[0]), .pin16(O[6]), .pin15(A[1]),
    .pin14(O[5]), .pin13(A[2]), .pin12(O[4]), .pin11(A[3]));
  _74244 #(.ShowInternalStructure("true")) u_74244_2 (
    .pin1(n74139_1_pin7), .pin2(and8_1_z[7]), .pin3(O[0]), .pin4(and8_1_z[6]), .pin5(O[1]),
    .pin6(and8_1_z[5]), .pin7(O[2]), .pin8(and8_1_z[4]), .pin9(O[3]), .pin19(n74139_1_pin7), .pin18(O[7]),
    .pin17(and8_1_z[0]), .pin16(O[6]), .pin15(and8_1_z[1]), .pin14(O[5]), .pin13(and8_1_z[2]), .pin12(O[4]),
    .pin11(and8_1_z[3]));
  // also tied to GND on the sheet: n74139_1_pin1

  // Notes on the sheet:
  //   00: A+B
  //   01: NOT A
  //   10: A - B
  //   11: A AND B
endmodule

module ADD (
  input  [7:0] X,
  input  [7:0] Y,
  input  CIN,
  output [7:0] Z,
  output CF
);

  wire n74283_1_pin7;

  _74283 #(.ShowInternalStructure("true")) u_74283_1 (
    .pin1(Z[5]), .pin2(X[5]), .pin3(Y[5]), .pin4(Z[4]), .pin5(X[4]), .pin6(Y[4]), .pin7(n74283_1_pin7),
    .pin15(Y[6]), .pin14(X[6]), .pin13(Z[6]), .pin12(X[7]), .pin11(Y[7]), .pin10(Z[7]), .pin9(CF));
  _74283 #(.ShowInternalStructure("true")) u_74283_2 (
    .pin1(Z[1]), .pin2(X[1]), .pin3(Y[1]), .pin4(Z[0]), .pin5(X[0]), .pin6(Y[0]), .pin7(CIN), .pin15(Y[2]),
    .pin14(X[2]), .pin13(Z[2]), .pin12(X[3]), .pin11(Y[3]), .pin10(Z[3]), .pin9(n74283_1_pin7));
endmodule

module INVERT (
  input  EN,
  input  [7:0] X,
  output [7:0] Z
);

  _7486 #(.ShowInternalStructure("true")) u_7486_1 (
    .pin1(EN), .pin2(X[4]), .pin3(Z[4]), .pin4(EN), .pin5(X[5]), .pin6(Z[5]), .pin13(EN), .pin12(X[7]),
    .pin11(Z[7]), .pin10(EN), .pin9(X[6]), .pin8(Z[6]));
  _7486 #(.ShowInternalStructure("true")) u_7486_2 (
    .pin1(EN), .pin2(X[0]), .pin3(Z[0]), .pin4(EN), .pin5(X[1]), .pin6(Z[1]), .pin13(EN), .pin12(X[3]),
    .pin11(Z[3]), .pin10(EN), .pin9(X[2]), .pin8(Z[2]));
endmodule

module PC (
  input  nRESET,
  input  CLK,
  input  [7:0] SET,
  input  nLOAD,
  output [7:0] ADDR
);

  wire n74163_1_pin7;

  _74163 #(.ShowInternalStructure("true")) u_74163_1 (
    .pin1(nRESET), .pin2(CLK), .pin3(SET[4]), .pin4(SET[5]), .pin5(SET[6]), .pin6(SET[7]),
    .pin7(n74163_1_pin7), .pin14(ADDR[4]), .pin13(ADDR[5]), .pin12(ADDR[6]), .pin11(ADDR[7]),
    .pin10(n74163_1_pin7), .pin9(nLOAD));  // open: pin15
  _74163 #(.ShowInternalStructure("true")) u_74163_2 (
    .pin1(nRESET), .pin2(CLK), .pin3(SET[0]), .pin4(SET[1]), .pin5(SET[2]), .pin6(SET[3]), .pin7(nRESET),
    .pin15(n74163_1_pin7), .pin14(ADDR[0]), .pin13(ADDR[1]), .pin12(ADDR[2]), .pin11(ADDR[3]),
    .pin10(nRESET), .pin9(nLOAD));
endmodule

module AND8 (
  input  [7:0] A,
  input  [7:0] B,
  output [7:0] Z
);

  _7408 #(.ShowInternalStructure("true")) u_7408_1 (
    .pin1(A[7]), .pin2(B[7]), .pin3(Z[7]), .pin4(A[6]), .pin5(B[6]), .pin6(Z[6]), .pin13(A[5]), .pin12(B[5]),
    .pin11(Z[5]), .pin10(A[4]), .pin9(B[4]), .pin8(Z[4]));
  _7408 #(.ShowInternalStructure("true")) u_7408_2 (
    .pin1(A[3]), .pin2(B[3]), .pin3(Z[3]), .pin4(A[2]), .pin5(B[2]), .pin6(Z[2]), .pin13(A[1]), .pin12(B[1]),
    .pin11(Z[1]), .pin10(A[0]), .pin9(B[0]), .pin8(Z[0]));
endmodule
